# Fritzing sketch Timelapse-Controller (saved by Fritzing 0.9.3b)
breadboards: 1

parts:
  Raspberry_Pi_1 = Raspberry Pi 3 [part_number=RPI-3-V1.2]
  IC1 = MCP3008 8-channel 10-bit ADC [part_number=MCP3008]
  R1 = Rotary Potentiometer (Small) [maximum_resistance=100kΩ package=THT]
  R2 = Rotary Potentiometer (Small) [maximum_resistance=100kΩ package=THT]
  S1 = Pushbutton [package="[THT]"]

nets:
  N1: Raspberry_Pi_1.3v3, IC1.no_name_yet#15, IC1.no_name_yet#16, R1.leg1, R2.leg1
  N2: Raspberry_Pi_1.GIPO17, S1.Pin_3, S1.Pin_4
  N3: Raspberry_Pi_1.GIPO10, IC1.no_name_yet#11
  N4: Raspberry_Pi_1.GIPO9, IC1.no_name_yet#12
  N5: Raspberry_Pi_1.GIPO11, IC1.no_name_yet#13
  N6: Raspberry_Pi_1.GIPO8, IC1.no_name_yet#10
  N7: Raspberry_Pi_1.GND, IC1.no_name_yet#9, IC1.no_name_yet#14, R1.leg2, R2.leg2, S1.Pin_1, S1.Pin_2
  N8: IC1.no_name_yet#1, R1.wiper
  N9: IC1.no_name_yet#2, R2.wiper
